# Fritzing sketch comprendre-encoder (saved by Fritzing 0.9.3b)

parts:
  Composant1 = Arduino Nano 33 IOT
  DC_Mot_Enc1 = DC Motor with two-phase hall-encoder [part_number=VT-E-G25A-06-177E]
  Composant2 = Adafruit TB6612 DC and Stepper Motor Driver [part_number="Adafruit #2448"]

nets:
  N1: Composant1.D3~, DC_Mot_Enc1.pin6
  N2: Composant1.D4, DC_Mot_Enc1.pin5
  N3: Composant1.D5~, Composant2.AIN2
  N4: Composant1.D6~, Composant2.AIN1
  N5: DC_Mot_Enc1.pin1, Composant2.MOTORA2
  N6: DC_Mot_Enc1.pin2, Composant2.MOTORA1

custom parts:
  Arduino Nano 33 IOT: The Arduino Nano 33 IoT is the easiest and cheapest point of entry to enhance existing devices (and creating new ones) to be part of the IoT and designing pico-network applications. Whether you are looking at building a sensor network connected to your office or home router, or if you want to create a BLE device sending data to a cellphone, the Nano 33 IoT is your one-stop-solution for many of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
  Adafruit TB6612 DC and Stepper Motor Driver: Spin two DC motors, step one bi-polar or uni-polar stepper, or fire off two solenoids with 1.2A per channel using the TB6612. These are perhaps better known as "the drivers in our assembled Adafruit Motorshield or Motor HAT." We really like these dual H-bridges, so if you want to control motors without a shield or HAT these are easy to include on any solderless breadboard or perma-proto.
