# Fritzing sketch moteur-hasheur (saved by Fritzing 0.9.3b)

parts:
  Composant1 = Arduino Nano 33 IOT
  DC_Mot_Enc1 = DC Motor with two-phase hall-encoder [part_number=VT-E-G25A-06-177E]
  L298N1 = L298N DC motor driver
  LiPo_11_1V_-_2350_mAh = LIPO-2000mAh [package=lipo-2000]  # not connected

nets:
  N1: Composant1.RESET, Composant1.A7, L298N1.IN4
  N2: Composant1.GND, Composant1.D13~, DC_Mot_Enc1.pin4
  N3: Composant1.D2, DC_Mot_Enc1.pin6
  N4: Composant1.D3~, Composant1.D4, DC_Mot_Enc1.pin5
  N5: Composant1.D11/MOSI, Composant1.+5V, DC_Mot_Enc1.pin3
  N6: Composant1.A6, L298N1.IN3
  N7: DC_Mot_Enc1.pin1, L298N1.OUT4
  N8: DC_Mot_Enc1.pin2, L298N1.OUT3

custom parts:
  Arduino Nano 33 IOT: The Arduino Nano 33 IoT is the easiest and cheapest point of entry to enhance existing devices (and creating new ones) to be part of the IoT and designing pico-network applications. Whether you are looking at building a sensor network connected to your office or home router, or if you want to create a BLE device sending data to a cellphone, the Nano 33 IoT is your one-stop-solution for many of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
  L298N DC motor driver: 2x DC motor driver with 78M05 positive voltage regulator (7..35 V) L298N: max 46 V, 2 A Set 5 V Enable jumper to enable 5 V regultor (needed for the L298N) and +5 V output at screw terminal or supply external +5 V at screw terminal Set ENA and/or ENB to +5 V to enable motor permanently or supply ENA and/or ENB with PWM signal IN1 and IN2 set rotation directory for motor A (OUT1/OUT2) IN2 and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
